# Fritzing sketch SmartLight Sketch (saved by Fritzing 0.9.3b)
breadboards: 3

parts:
  Bauteil1 = Arduino Uno (Rev3)
  R1 = Rotary Potentiometer (Small) [maximum_resistance=100kΩ package=THT]
  R2 = Rotary Potentiometer (Small) [maximum_resistance=100kΩ package=THT]
  R3 = Rotary Potentiometer (Small) [maximum_resistance=100kΩ package=THT]
  LCD1 = LCD screen
  Grove1 = Grove Temperature Sensor
  PIR2 = PIR sensor
  Grove2 = Grove Light Sensor
  R4 = Resistor [tolerance=±5% resistance=220 package=THT]
  J1 = Piezo Speaker
  Part3 = 12 NeoPixel Ring [part_number=1643]

nets:
  N1: Bauteil1.A1, Grove2.SIG
  N2: Bauteil1.A2, Grove1.SIG
  N3: Bauteil1.A3, R2.wiper
  N4: Bauteil1.A4/SDA, R3.wiper
  N5: Bauteil1.D8, Part3.IN
  N6: Bauteil1.D11_PWM/MOSI, LCD1.E
  N7: Bauteil1.D12/MISO, LCD1.RS
  N8: Bauteil1.D2, LCD1.DB7
  N9: Bauteil1.D3_PWM, LCD1.DB6
  N10: Bauteil1.D4, LCD1.DB5
  N11: Bauteil1.D5_PWM, LCD1.DB4
  N12: Bauteil1.D6_PWM, PIR2.SIG
  VDD: Bauteil1.5V, R1.leg1, R2.leg1, R3.leg1, LCD1.VDD, Grove1.VCC, PIR2.VDD, Grove2.VCC, R4.Pin_0, Part3.VDD
  GND: Bauteil1.GND, R1.leg2, R2.leg2, R3.leg2, LCD1.VSS, LCD1.R/W, LCD1.LED-, Grove1.GND, PIR2.GND, Grove2.GND, J1.pin1, Part3.GND
  N13: R1.wiper, LCD1.V0
  N14: LCD1.LED+, R4.Pin_1

notes:
  Regler:
  1. Helligkeitsregler für LED
  2. Farbregler für LED
  3. Helligkeitsregler für LCD
  Sensoren:
  1. Helligkeitssensor
  2. Temperatursensor
  3. Bewegungssensor
  Aktoren:
  1. Lautsprecher
  2. Neopixel (12 LEDs)
  3. LCD-Display (4x20)

custom parts:
  Grove Light Sensor: An analog light sensor
  12 NeoPixel Ring: 12 ultra bright smart LED NeoPixels are arranged in a circle with 1.5" (37mm) outer diameter. The rings are 'chainable' - connect the output pin of one to the input pin of another. Use only one microcontroller pin to control as many as you can chain together! Each LED is addressable as the driver chip is inside the LED. Each one has ~18mA constant current drive so the color will be very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
